# Fritzing sketch circuit (saved by Fritzing 0.9.3b)
breadboards: 1

parts:
  Raspberry_Pi_1 = Raspberry Pi 3 [part_number=RPI-3-V1.2]
  Bauteil1 = ws2812b [package="smd 2812b"]
  Power_supply = Power plug [part_number="5V DC"]
  Bauteil2 = ws2812b [package="smd 2812b"]
  Bauteil3 = ws2812b [package="smd 2812b"]
  Bauteil4 = ws2812b [package="smd 2812b"]

nets:
  N1: Raspberry_Pi_1.GPIO24, Bauteil1.DIN
  VSS: Raspberry_Pi_1.GND, Bauteil1.VSS, Power_supply.GND, Bauteil2.VSS, Bauteil3.VSS, Bauteil4.VSS
  VDD: Bauteil1.VDD, Power_supply.VCC, Bauteil2.VDD, Bauteil3.VDD, Bauteil4.VDD
  N2: Bauteil1.DOUT, Bauteil2.DIN
  N3: Bauteil2.DOUT, Bauteil3.DIN
  N4: Bauteil3.DOUT, Bauteil4.DIN
